# Fritzing sketch CeilingFan (saved by Fritzing 0.9.10b)
circuit board: 15.8891cm x 8.04337cm
breadboards: 1

parts:
  ESP8266 = Amica NodeMCU DEVKIT 1.0
  PCA9685 = PCA9685 16x12-bit PWM Breakout
  Relay_module = Module 4 Relais 5V [package="Module 4 Relais 5V"]
  J1 = female pin header, 15 pins [form="♀ (female)"]
  J2 = female pin header, 15 pins [form="♀ (female)"]

nets:
  N1: ESP8266.pin1, ESP8266.pin_10, ESP8266.pin_26, PCA9685.no_name_yet#505, J1.pin6, J1.pin15, J2.pin11
  N2: ESP8266.pin2, ESP8266.pin_9, ESP8266.pin_25, ESP8266.pin_29, PCA9685.no_name_yet#501, PCA9685.no_name_yet#1000, Relay_module.GND, J1.pin7, J1.pin14, J2.pin10, J2.pin14
  N3: ESP8266.pin3, J1.pin13
  N4: ESP8266.pin4, J1.pin12
  N5: ESP8266.pin5, Relay_module.IN4, J1.pin11
  N6: ESP8266.pin6, Relay_module.IN2, J1.pin10
  N7: ESP8266.pin7, Relay_module.IN1, J1.pin9
  N8: ESP8266.pin8, Relay_module.IN3, J1.pin8
  N9: ESP8266.pin_11, J1.pin5
  N10: ESP8266.pin_12, J1.pin4
  N11: ESP8266.pin_13, PCA9685.no_name_yet#504, J1.pin3
  N12: ESP8266.pin_14, PCA9685.no_name_yet#503, J1.pin2
  N13: ESP8266.pin_15, J1.pin1
  N14: ESP8266.pin_16, J2.pin1
  N15: ESP8266.pin_17, J2.pin2
  N16: ESP8266.pin_18, J2.pin3
  N17: ESP8266.pin_19, J2.pin4
  N18: ESP8266.pin_20, J2.pin5
  N19: ESP8266.pin_21, J2.pin6
  N20: ESP8266.pin_22, J2.pin7
  N21: ESP8266.pin_23, J2.pin8
  N22: ESP8266.pin_24, J2.pin9
  N23: ESP8266.pin_27, J2.pin12
  N24: ESP8266.pin_28, J2.pin13
  N25: ESP8266.pin_30, Relay_module.VCC, J2.pin15

custom parts:
  Module 4 Relais 5V: Module 4 Relais 5V 4x SPD-06VDC-SD-C
